// Logisim project ex1_circuit.circ as structural Verilog: 6 circuits, main circuit main
module main (
  input  in_1,
  input  in_2,
  output out_3
);

  NAND1 nand1_1 (.input1(in_1), .input2(in_2), .output1(out_3));
  // NAND_Gate nand_1 is placed but not wired
endmodule

module NAND1 (
  input  input1,
  input  input2,
  output output1
);

  wire and_1_out;

  and and_1 (and_1_out, input1, input2);
  not not_1 (output1, and_1_out);
endmodule

module NOR1 (
  input  in_1,
  input  in_2,
  output out_3
);

  wire or_1_out;

  or or_1 (or_1_out, in_1, in_2);
  not not_1 (out_3, or_1_out);
endmodule

module XOR1 (
  input  in_1,
  input  in_2,
  output out_3
);

  wire and_1_out, and_2_out, not_1_out, not_2_out;

  not not_1 (not_1_out, in_1);
  not not_2 (not_2_out, in_2);
  and and_1 (and_1_out, not_1_out, in_2);
  and and_2 (and_2_out, in_1, not_2_out);
  or or_1 (out_3, and_1_out, and_2_out);
endmodule

module Muxtwo1 (
  input  input1,
  input  S,
  input  input2,
  output out_4
);

  wire and_1_out, and_2_out, not_1_out;

  not not_1 (not_1_out, S);
  and and_1 (and_1_out, not_1_out, input1);
  and and_2 (and_2_out, S, input2);
  or or_1 (out_4, and_1_out, and_2_out);
endmodule

module Muxfour2 (
  input  input1,
  input  input2,
  input  input3,
  input  input4,
  input  [1:0] S,
  output out_6
);

  wire muxtwo1_1_out_4, muxtwo1_2_out_4;

  Muxtwo1 muxtwo1_1 (.input1(input1), .S(S[0]), .input2(input2), .out_4(muxtwo1_1_out_4));
  Muxtwo1 muxtwo1_2 (.input1(input3), .S(S[0]), .input2(input4), .out_4(muxtwo1_2_out_4));
  Muxtwo1 muxtwo1_3 (.input1(muxtwo1_1_out_4), .S(S[1]), .input2(muxtwo1_2_out_4), .out_4(out_6));
endmodule
