// Logisim project ex2_circuit.circ as structural Verilog: 2 circuits, main circuit main
module main (
);

  AddMachine addmachine_1 ();  // open: out_1, out_2
endmodule

module AddMachine (
  output [7:0] out_1,
  output [7:0] out_2
);

  wire clock_1_out;

  Adder adder_1 (.a(8'h1), .b(out_2), .out(out_1));  // open: cin, cout
  Clock clock_1 (.out(clock_1_out));
  // Probe on out_2
  // Probe on out_1
  Register register_1 (.D(out_1), .clk(clock_1_out), .Q(out_2));  // open: en, clr
endmodule
