// Logisim project ex4_circuit.circ as structural Verilog
module ex4 (
  input  [7:0] IN1,
  output [7:0] out1,
  output [7:0] out2
);

  wire and_1_out;

  not not_1 (out2[7], IN1[7]);
  and and_1 (and_1_out, IN1[0], IN1[7]);
  assign out1 = {{7{and_1_out}}, and_1_out};  // Bit_Extender bit_extender_1

  assign out2[6:0] = IN1[6:0];
endmodule
