// Logisim project ex5_circuit.circ as structural Verilog
module ex5 (
  input  [15:0] A,
  input  [3:0] B,
  output [15:0] out_3
);

  wire [15:0] eight_shift_1_out_2, four_shift_1_out_2, multiplexer_1_out, multiplexer_2_out,
       multiplexer_3_out, one_shift_1_out_2, two_shift_1_out_2;

  one_shift one_shift_1 (.in_1(A), .out_2(one_shift_1_out_2));
  Multiplexer #(.width(16), .enable("false")) multiplexer_1 (
    .in0(A), .in1(one_shift_1_out_2), .out(multiplexer_1_out), .sel(B[0]));
  two_shift two_shift_1 (.in_1(A), .out_2(two_shift_1_out_2));
  Multiplexer #(.width(16), .enable("false")) multiplexer_2 (
    .in0(multiplexer_1_out), .in1(two_shift_1_out_2), .out(multiplexer_2_out), .sel(B[1]));
  four_shift four_shift_1 (.in_1(A), .out_2(four_shift_1_out_2));
  Multiplexer #(.width(16), .enable("false")) multiplexer_3 (
    .in0(multiplexer_2_out), .in1(four_shift_1_out_2), .out(multiplexer_3_out), .sel(B[2]));
  eight_shift eight_shift_1 (.in_1(A), .out_2(eight_shift_1_out_2));
  Multiplexer #(.width(16), .enable("false")) multiplexer_4 (
    .in0(multiplexer_3_out), .in1(eight_shift_1_out_2), .out(out_3), .sel(B[3]));
endmodule

module one_shift (
  input  [15:0] in_1,
  output [15:0] out_2
);


  assign out_2 = {in_1[0], in_1[15:1]};
endmodule

module two_shift (
  input  [15:0] in_1,
  output [15:0] out_2
);

  wire [15:0] one_shift_1_out_2;

  one_shift one_shift_1 (.in_1(in_1), .out_2(one_shift_1_out_2));
  one_shift one_shift_2 (.in_1(one_shift_1_out_2), .out_2(out_2));
endmodule

module four_shift (
  input  [15:0] in_1,
  output [15:0] out_2
);

  wire [15:0] two_shift_1_out_2;

  Multiplexer #(.enable("false")) multiplexer_1 ();  // open: in0, in1, out, sel
  two_shift two_shift_1 (.in_1(in_1), .out_2(two_shift_1_out_2));
  two_shift two_shift_2 (.in_1(two_shift_1_out_2), .out_2(out_2));
endmodule

module eight_shift (
  input  [15:0] in_1,
  output [15:0] out_2
);

  wire [15:0] four_shift_1_out_2;

  four_shift four_shift_1 (.in_1(in_1), .out_2(four_shift_1_out_2));
  four_shift four_shift_2 (.in_1(four_shift_1_out_2), .out_2(out_2));
endmodule
